// Logisim project 21.circ as structural Verilog: 4 circuits, main circuit main
module main (
  input  W,
  output Z
);

  wire clock_1_out;
  wire [6:0] next_state_1_snext, register_1_q;

  next_state next_state_1 (.S(register_1_q), .W(W), .Snext(next_state_1_snext));
  Register #(.width(7)) register_1 (
    .D(next_state_1_snext), .en(1'b1), .clk(clock_1_out), .Q(register_1_q));  // open: clr
  Clock clock_1 (.out(clock_1_out));
  output_logic output_logic_1 (.S(register_1_q), .Z(Z));
endmodule

module next_state (
  input  [6:0] S,
  input  W,
  output [6:0] Snext
);

  wire comparator_1_eq, not_1_out, not_2_out, or_1_out, or_2_out, or_3_out, or_4_out, or_5_out;

  Comparator #(.mode("unsigned"), .width(7)) comparator_1 (.a({7{1'b0}}), .b(S), .eq(comparator_1_eq));  // open: gt, lt
  or or_1 (or_1_out, S[0], comparator_1_eq);
  not not_1 (not_1_out, W);
  or or_2 (or_2_out, or_1_out, S[1], S[4], S[6]);
  and and_1 (Snext[1], W, or_1_out);
  or or_3 (or_3_out, S[1], S[6]);
  and and_2 (Snext[3], W, S[2]);
  not not_2 (not_2_out, W);
  or or_4 (or_4_out, S[2], S[3], S[5]);
  or or_5 (or_5_out, S[5], S[3]);
  and and_3 (Snext[6], W, S[4]);
  and and_4 (Snext[0], not_1_out, or_2_out);
  and and_5 (Snext[2], W, or_3_out);
  and and_6 (Snext[4], not_2_out, or_4_out);
  and and_7 (Snext[5], W, or_5_out);
endmodule

module output_logic (
  input  [6:0] S,
  output Z
);

  or or_1 (Z, S[5], S[6]);
endmodule

module one_hot_reg_7 (
  input  [6:0] D,
  input  Clock,
  input  Reset,
  output [6:0] Q
);

  D_Flip_Flop d_ff_1 (.D(D[0]), .clk(Clock), .Q(Q[0]), .preset(Reset));  // open: Qn, reset
  D_Flip_Flop d_ff_2 (.D(D[1]), .clk(Clock), .Q(Q[1]), .reset(Reset));  // open: Qn, preset
  D_Flip_Flop d_ff_3 (.D(D[2]), .clk(Clock), .Q(Q[2]), .reset(Reset));  // open: Qn, preset
  D_Flip_Flop d_ff_4 (.D(D[3]), .clk(Clock), .Q(Q[3]), .reset(Reset));  // open: Qn, preset
  D_Flip_Flop d_ff_5 (.D(D[4]), .clk(Clock), .Q(Q[4]), .reset(Reset));  // open: Qn, preset
  D_Flip_Flop d_ff_6 (.D(D[5]), .clk(Clock), .Q(Q[5]), .reset(Reset));  // open: Qn, preset
  D_Flip_Flop d_ff_7 (.D(D[6]), .clk(Clock), .Q(Q[6]), .reset(Reset));  // open: Qn, preset
endmodule
